# Fritzing sketch SimonSays (saved by Fritzing 0.8.7b)
breadboards: 2

parts:
  S1 = Pushbutton [package="[THT]"]
  S2 = Pushbutton [package="[THT]"]
  S3 = Pushbutton [package="[THT]"]
  S4 = Pushbutton [package="[THT]"]
  LED1 = LED - 5mm [color="Red (633nm)" package="5 mm [THT]"]
  LED2 = LED - 5mm [color="Yellow (574nm)" package="5 mm [THT]"]
  LED3 = LED - 5mm [color="Green (555nm)" package="5 mm [THT]"]
  LED4 = LED - 5mm [color="Blue (430nm)" package="5 mm [THT]"]
  R1 = Resistor [tolerance=±5% resistance=220 package=THT]
  R2 = Resistor [tolerance=±5% resistance=220 package=THT]
  R3 = Resistor [tolerance=±5% resistance=220 package=THT]
  R4 = Resistor [tolerance=±5% resistance=220 package=THT]
  Bauteil1 = Arduino Uno (Rev3)

nets:
  N1: S1.Pin_1, S1.Pin_2, Bauteil1.D4
  N2: S1.Pin_3, S1.Pin_4, S2.Pin_3, S2.Pin_4, S3.Pin_3, S3.Pin_4, S4.Pin_3, S4.Pin_4, R1.Pin_1, R2.Pin_1, R3.Pin_1, R4.Pin_1, Bauteil1.GND
  N3: S2.Pin_1, S2.Pin_2, Bauteil1.D5_PWM
  N4: S3.Pin_1, S3.Pin_2, Bauteil1.D6_PWM
  N5: S4.Pin_1, S4.Pin_2, Bauteil1.D7
  N6: LED1.cathode, R1.Pin_0
  N7: LED1.anode, Bauteil1.D8
  N8: LED2.cathode, R2.Pin_0
  N9: LED2.anode, Bauteil1.D9_PWM
  N10: LED3.cathode, R3.Pin_0
  N11: LED3.anode, Bauteil1.D10_PWM/SS
  N12: LED4.cathode, R4.Pin_0
  N13: LED4.anode, Bauteil1.D11_PWM/MOSI
